# Fritzing sketch 01_02_blink (saved by Fritzing 0.9.1b)
breadboards: 1

parts:
  TRINKET1 = Trinket 3V
  LED1 = LED - 3mm [color="Red (633nm)" package="3 mm [THT]"]
  R1 = Resistor [tolerance=±5% resistance=220 package="1206 [SMD]"]
  BAT1 = Battery Holders [package=battery_20mm_pth_compact]

nets:
  N1: TRINKET1.no_name_yet#1, BAT1.+
  N2: TRINKET1.no_name_yet#2, R1.Pin_1, BAT1.-
  N3: TRINKET1.no_name_yet#9, LED1.anode
  N4: LED1.cathode, R1.Pin_0

custom parts:
  Trinket 3V: Adafruit Trinket 3V

// code stored in the sketch: _05_simple_led_w_trinket.ino
void setup() {
  pinMode(0, OUTPUT);
}

void loop() {
  digitalWrite(0, HIGH); 
    delay(1000);
    digitalWrite(0, LOW);
    delay(1000);
}
