# Fritzing sketch 03_wake_up_knock (saved by Fritzing 0.9.1b)
breadboards: 1

parts:
  Adafruit_Trinket = Trinket 3V
  LED1 = LED - 3mm [color="Red (660nm)" package="3 mm [THT]"]
  R1 = Resistor [tolerance=±5% resistance=200 package="1206 [SMD]"]
  BAT1 = Battery Holders [package=battery_20mm_pth_compact]
  Piezo = Piezo Speaker
  R2 = Resistor [tolerance=±5% resistance=120k package="0805 [SMD]"]

nets:
  N1: Adafruit_Trinket.no_name_yet#1, BAT1.+
  N2: Adafruit_Trinket.no_name_yet#2, R1.Pin_1, BAT1.-, Piezo.pin1, R2.Pin_1
  N3: Adafruit_Trinket.no_name_yet#7, Piezo.pin2, R2.Pin_0
  N4: Adafruit_Trinket.no_name_yet#9, LED1.anode
  N5: LED1.cathode, R1.Pin_0

custom parts:
  Trinket 3V: Adafruit Trinket 3V

// code stored in the sketch: _03_wake_up_knock.ino
#define LED_PIN 0

#define PIEZO_PIN 2


const int knockFadeTime = 500;
             
byte piezoValue = 0;
int ledState = LOW;
int THRESHOLD = 95;

void setup() {
  pinMode(LED_PIN, OUTPUT);
  pinMode(PIEZO_PIN, INPUT);
}


void loop() {
  piezoValue = analogRead(PIEZO_PIN);     
  if (piezoValue >= THRESHOLD) {
    ledState = !ledState;
    digitalWrite(LED_PIN, ledState);
    knockDelay();
  }
}

void knockDelay(){
  int itterations = (knockFadeTime / 20);      // Wait for the peak to dissipate before listening to next one.
  for (int i=0; i < itterations; i++){
    delay(10);
    analogRead(PIEZO_PIN);                  // This is done in an attempt to defuse the analog sensor's capacitor that will give false readings on high impedance sensors.
    delay(10);
  } 
}

// code stored in the sketch: _05_simple_led_w_trinket.ino
void setup() {
  pinMode(0, OUTPUT);
}

void loop() {
  digitalWrite(0, HIGH); 
    delay(1000);
    digitalWrite(0, LOW);
    delay(1000);
}
