# Fritzing sketch 06_charlieplexing (saved by Fritzing 0.9.1b)
breadboards: 1

parts:
  Adafruit_Trinket = Trinket 3V
  R1 = Resistor [tolerance=±5% resistance=51 package="1206 [SMD]"]
  Battery = Battery Holders [package=battery_20mm_pth_compact]
  AB = LED - 3mm [color="Red (660nm)" package="3 mm [THT]"]
  BA = LED - 3mm [color="Red (660nm)" package="3 mm [THT]"]
  BC = LED - 3mm [color="Red (660nm)" package="3 mm [THT]"]
  CB = LED - 3mm [color="Red (660nm)" package="3 mm [THT]"]
  AC = LED - 3mm [color="Red (660nm)" package="3 mm [THT]"]
  CA = LED - 3mm [color="Red (660nm)" package="3 mm [THT]"]
  DA = LED - 3mm [color="Red (660nm)" package="3 mm [THT]"]
  AD = LED - 3mm [color="Red (660nm)" package="3 mm [THT]"]
  BD = LED - 3mm [color="Red (660nm)" package="3 mm [THT]"]
  DB = LED - 3mm [color="Red (660nm)" package="3 mm [THT]"]
  CD = LED - 3mm [color="Red (660nm)" package="3 mm [THT]"]
  DC = LED - 3mm [color="Red (660nm)" package="3 mm [THT]"]
  R2 = Resistor [tolerance=±5% resistance=51 package="1206 [SMD]"]
  R3 = Resistor [tolerance=±5% resistance=51 package="1206 [SMD]"]
  R4 = Resistor [tolerance=±5% resistance=51 package="1206 [SMD]"]

nets:
  N1: Adafruit_Trinket.no_name_yet#1, Battery.+
  N2: Adafruit_Trinket.no_name_yet#2, Battery.-
  N3: Adafruit_Trinket.no_name_yet#3, R3.Pin_1
  N4: Adafruit_Trinket.no_name_yet#4, R4.Pin_1
  N5: Adafruit_Trinket.no_name_yet#7, R2.Pin_0
  N6: Adafruit_Trinket.no_name_yet#9, R1.Pin_0
  N7: R1.Pin_1, AB.anode, BA.cathode, AC.anode, CA.cathode, DA.cathode, AD.anode
  N8: AB.cathode, BA.anode, BC.anode, CB.cathode, BD.cathode, DB.anode, R2.Pin_1
  N9: BC.cathode, CB.anode, AC.cathode, CA.anode, CD.anode, DC.cathode, R3.Pin_0
  N10: DA.anode, AD.cathode, BD.anode, DB.cathode, CD.cathode, DC.anode, R4.Pin_0

custom parts:
  Trinket 3V: Adafruit Trinket 3V

// code stored in the sketch: _03_wake_up_knock.ino
#define LED_PIN 0

#define PIEZO_PIN 2


const int knockFadeTime = 500;
             
byte piezoValue = 0;
int ledState = LOW;
int THRESHOLD = 95;

void setup() {
  pinMode(LED_PIN, OUTPUT);
  pinMode(PIEZO_PIN, INPUT);
}


void loop() {
  piezoValue = analogRead(PIEZO_PIN);     
  if (piezoValue >= THRESHOLD) {
    ledState = !ledState;
    digitalWrite(LED_PIN, ledState);
    knockDelay();
  }
}

void knockDelay(){
  int itterations = (knockFadeTime / 20);      // Wait for the peak to dissipate before listening to next one.
  for (int i=0; i < itterations; i++){
    delay(10);
    analogRead(PIEZO_PIN);                  // This is done in an attempt to defuse the analog sensor's capacitor that will give false readings on high impedance sensors.
    delay(10);
  } 
}

// code stored in the sketch: _05_melody.ino
#define NOTE_B0  31
#define NOTE_C1  33
#define NOTE_CS1 35
#define NOTE_D1  37
#define NOTE_DS1 39
#define NOTE_E1  41
#define NOTE_F1  44
#define NOTE_FS1 46
#define NOTE_G1  49
#define NOTE_GS1 52
#define NOTE_A1  55
#define NOTE_AS1 58
#define NOTE_B1  62
#define NOTE_C2  65
#define NOTE_CS2 69
#define NOTE_D2  73
#define NOTE_DS2 78
#define NOTE_E2  82
#define NOTE_F2  87
#define NOTE_FS2 93
#define NOTE_G2  98
#define NOTE_GS2 104
#define NOTE_A2  110
#define NOTE_AS2 117
#define NOTE_B2  123
#define NOTE_C3  131
#define NOTE_CS3 139
#define NOTE_D3  147
#define NOTE_DS3 156
#define NOTE_E3  165
#define NOTE_F3  175
#define NOTE_FS3 185
#define NOTE_G3  196
#define NOTE_GS3 208
#define NOTE_A3  220
#define NOTE_AS3 233
#define NOTE_B3  247
#define NOTE_C4  262
#define NOTE_CS4 277
#define NOTE_D4  294
#define NOTE_DS4 311
#define NOTE_E4  330
#define NOTE_F4  349
#define NOTE_FS4 370
#define NOTE_G4  392
#define NOTE_GS4 415
#define NOTE_A4  440
#define NOTE_AS4 466
#define NOTE_B4  494
#define NOTE_C5  523
#define NOTE_CS5 554
#define NOTE_D5  587
#define NOTE_DS5 622
#define NOTE_E5  659
#define NOTE_F5  698
#define NOTE_FS5 740
#define NOTE_G5  784
#define NOTE_GS5 831
#define NOTE_A5  880
#define NOTE_AS5 932
#define NOTE_B5  988
#define NOTE_C6  1047
#define NOTE_CS6 1109
#define NOTE_D6  1175
#define NOTE_DS6 1245
#define NOTE_E6  1319
#define NOTE_F6  1397
#define NOTE_FS6 1480
#define NOTE_G6  1568
#define NOTE_GS6 1661
#define NOTE_A6  1760
#define NOTE_AS6 1865
#define NOTE_B6  1976
#define NOTE_C7  2093
#define NOTE_CS7 2217
#define NOTE_D7  2349
#define NOTE_DS7 2489
#define NOTE_E7  2637
#define NOTE_F7  2794
#define NOTE_FS7 2960
#define NOTE_G7  3136
#define NOTE_GS7 3322
#define NOTE_A7  3520
#define NOTE_AS7 3729
#define NOTE_B7  3951
#define NOTE_C8  4186
#define NOTE_CS8 4435
#define NOTE_D8  4699
#define NOTE_DS8 4978
 
#define LED_PIN 0
#define PIEZO_PIN 2

int melody[] = {
  NOTE_E7, NOTE_E7, 0, NOTE_E7, 0, NOTE_C7, NOTE_E7, 0,
  NOTE_G7, 0, 0, 0, NOTE_G6, 0, 0, 0,
 
  NOTE_C7, 0, 0, NOTE_G6, 0, 0, NOTE_E6, 0,
  0, NOTE_A6, 0, NOTE_B6, 0, NOTE_AS6, NOTE_A6, 0,
 
  NOTE_G6, NOTE_E7, NOTE_G7, NOTE_A7, 0, NOTE_F7, NOTE_G7,
  0, NOTE_E7, 0, NOTE_C7, NOTE_D7, NOTE_B6, 0, 0,
 
  NOTE_C7, 0, 0, NOTE_G6, 0, 0, NOTE_E6, 0,
  0, NOTE_A6, 0, NOTE_B6, 0, NOTE_AS6, NOTE_A6, 0,
 
  NOTE_G6, NOTE_E7, NOTE_G7, NOTE_A7, 0, NOTE_F7, NOTE_G7,
  0, NOTE_E7, 0, NOTE_C7, NOTE_D7, NOTE_B6, 0, 0
};

//Mario main them tempo
int tempo[] = {
  12, 12, 12, 12, 12, 12, 12, 12,
  12, 12, 12, 12, 12, 12, 12, 12,
 
  12, 12, 12, 12, 12, 12, 12, 12,
  12, 12, 12, 12, 12, 12, 12, 12,
 
  9, 9, 9, 12, 12, 12, 12,
  12, 12, 12, 12, 12, 12, 12, 12,
 
  12, 12, 12, 12, 12, 12, 12, 12,
  12, 12, 12, 12, 12, 12, 12, 12,
 
  9, 9, 9, 12, 12, 12, 12,
  12, 12, 12, 12, 12, 12, 12, 12,
};
 
void setup(void)
{
  pinMode(PIEZO_PIN, OUTPUT);//buzzer
  pinMode(LED_PIN, OUTPUT);//led indicator when singing a note
 
}
void loop()
{ 
  int size = sizeof(melody) / sizeof(int);
  for (int thisNote = 0; thisNote < size; thisNote++) {
 
    // to calculate the note duration, take one second
    // divided by the note type.
    //e.g. quarter note = 1000 / 4, eighth note = 1000/8, etc.
    int noteDuration = 1000 / tempo[thisNote];
 
    buzz(PIEZO_PIN, melody[thisNote], noteDuration);
 
    // to distinguish the notes, set a minimum time between them.
    // the note's duration + 30% seems to work well:
    int pauseBetweenNotes = noteDuration * 1.30;
    delay(pauseBetweenNotes);
 
    // stop the tone playing:
    buzz(PIEZO_PIN, 0, noteDuration);
  }
}
 
void buzz(int targetPin, long frequency, long length) {
  digitalWrite(LED_PIN, HIGH);
  long delayValue = 1000000 / frequency / 2; // calculate the delay value between transitions
  //// 1 second's worth of microseconds, divided by the frequency, then split in half since
  //// there are two phases to each cycle
  long numCycles = frequency * length / 1000; // calculate the number of cycles for proper timing
  //// multiply frequency, which is really cycles per second, by the number of seconds to
  //// get the total number of cycles to produce
  for (long i = 0; i < numCycles; i++) { // for the calculated length of time...
    digitalWrite(targetPin, HIGH); // write the buzzer pin high to push out the diaphram
    delayMicroseconds(delayValue); // wait for the calculated delay value
    digitalWrite(targetPin, LOW); // write the buzzer pin low to pull back the diaphram
    delayMicroseconds(delayValue); // wait again or the calculated delay value
  }
  digitalWrite(LED_PIN, LOW);
 
}

// code stored in the sketch: _05_simple_led_w_trinket.ino
void setup() {
  pinMode(0, OUTPUT);
}

void loop() {
  digitalWrite(0, HIGH); 
    delay(1000);
    digitalWrite(0, LOW);
    delay(1000);
}
